# Fritzing sketch Borewell v01 (saved by Fritzing 0.9.10b)
circuit board: 13.0952cm x 9.1628cm
breadboards: 1

parts:
  OLED = Grove OLED 128x96
  Mod1 = Amica NodeMCU DEVKIT 1.0
  Mag_Sensor = female pin header, 3 pins [form="♀ (female)"]
  Mega = Arduino Mega 2560 (Rev3)
  Motor_Driver_L298N = female pin header, 4 pins [form="♀ (female)"]
  SIM800L = SIM800L [package=THT]
  Switch = Square Pushbutton
  J1 = Basic Servo

nets:
  GND: OLED.GND, Mod1.pin2, Mod1.pin_9, Mod1.pin_29, Mag_Sensor.pin2, Mega.GND, SIM800L.GND, J1.gnd
  VCC: OLED.VCC, Mag_Sensor.pin3, Mega.IOREF, SIM800L.5V, J1.vcc
  N1: OLED.SDA, Mega.D21/SCL, Mega.SCL
  N2: OLED.SCL, Mega.D20/SDA, Mega.SDA
  N3: Mod1.pin3, Mega.D0_RX0
  N4: Mod1.pin4, Mega.D1_TX0
  N5: Mag_Sensor.pin1, Mega.A0
  N6: Mega.A1, Switch.leg1
  N7: Mega.D19/RX1, SIM800L.SIM_TXD
  N8: Mega.D18/TX1, SIM800L.SIM_RXD
  N9: Mega.5V, Switch.leg0
  N10: Mega.D2_PWM, Motor_Driver_L298N.pin3
  N11: Mega.D3_PWM, Motor_Driver_L298N.pin4
  N12: Mega.D4_PWM, Motor_Driver_L298N.pin2
  N13: Mega.D5_PWM, Motor_Driver_L298N.pin1
  N14: Mega.D6_PWM, J1.pulse

notes:
  Designed by gwsisland.org
  Borewell Proto v01
