# Fritzing sketch GWS RechargeWell PCB (saved by Fritzing 0.9.10b)
circuit board: 7.18909cm x 6.81732cm
breadboards: 1

parts:
  OLED = Grove OLED 128x96
  SIM800L = SIM800L [package=THT]
  Arduino = Arduino Uno (Rev3) - ICSP
  MOLEX = Header 6 [package=molex-1x6-ra_lock]

nets:
  GND: OLED.GND, SIM800L.GND, Arduino.GND
  5V: OLED.VCC, SIM800L.5V, Arduino.5V, MOLEX.1
  N1: OLED.SDA, Arduino.A4/SDA
  N2: OLED.SCL, Arduino.A5/SCL
  N3: SIM800L.SIM_TXD, Arduino.D0/RX
  N4: SIM800L.SIM_RXD, Arduino.D1/TX
  N5: Arduino.A0, MOLEX.5
  N6: Arduino.A1, MOLEX.4
  N7: Arduino.A2, MOLEX.3
  N8: Arduino.A3, MOLEX.2

notes:
  Designed by gwsisland.org
  RechargeWell Proto v01
